# Fritzing sketch 04 (saved by Fritzing 0.9.3b)
breadboards: 1

parts:
  LCD1 = LCD screen
  Súčiastka1 = Arduino Uno (Rev3)
  R1 = Rotary Potentiometer (Small) [maximum_resistance=100kΩ package=THT]

nets:
  VSS: LCD1.VSS, LCD1.R/W, LCD1.LED-, Súčiastka1.GND, R1.leg2
  VDD: LCD1.VDD, LCD1.LED+, Súčiastka1.5V, R1.leg1
  N1: LCD1.V0, R1.wiper
  N2: LCD1.RS, Súčiastka1.D2
  N3: LCD1.E, Súčiastka1.D3_PWM
  N4: LCD1.DB4, Súčiastka1.D6_PWM
  N5: LCD1.DB5, Súčiastka1.D7
  N6: LCD1.DB6, Súčiastka1.D8
  N7: LCD1.DB7, Súčiastka1.D9_PWM
